// Logisim project SAP-1.circ as structural Verilog: 11 circuits, main circuit SAP-1
// OO
module SAP_1 (
  input  in_1,
  input  in_2,
  input  [3:0] in_3,
  input  [7:0] in_4
);

  wire AI, AO, BI, CE, CF, Clk, clock_1_out, clock_2_cycle_led, Clr, CO, EO, FI, Halt, II, IO, Jump, MI,
       MI_t, nClk, OI, RI, RO, Step, SU, Write, ZF;
  wire [3:0] Digit_1, Digit_2, Digit_3, instruction_register_1_optcode_output,
       memory_address_register_1_address_output, memory_address_register_1_memory_output_led,
       program_counter_1_out_7;
  wire [4:0] control_logic_1_cycle_led;
  wire [7:0] alu_1_out_8, Bus, instruction_register_1_instruction_output_led, out_register_1_out_led,
       ram_1_out_9, registre_a_1_alu_output, registre_a_1_led_output, registre_b_1_alu_output,
       registre_b_1_led_output;

  LED T0 (.in(control_logic_1_cycle_led[4]));
  LED T1 (.in(control_logic_1_cycle_led[3]));
  Button button_1 (.out(Step));
  Button button_2 (.out(Clr));
  LED T3 (.in(control_logic_1_cycle_led[1]));
  LED T2 (.in(control_logic_1_cycle_led[2]));
  LED T4 (.in(control_logic_1_cycle_led[0]));
  Control_Logic control_logic_1 (
    .Clk(nClk), .Optcode_Input(instruction_register_1_optcode_output), .Clr(Clr), .AI(AI), .AO(AO), .BI(BI),
    .FI(FI), .EO(EO), .Cycle_Led(control_logic_1_cycle_led), .SU(SU), .CO(CO), .CE(CE), .Jump(Jump), .RI(RI),
    .RO(RO), .Halt(Halt), .OI(OI), .MI(MI), .II(II), .IO(IO), .Carry(CF), .Zero(ZF));
  Button button_3 (.out(Write));
  Clock_part clock_1 (.out(clock_1_out));
  LED led_1 (.in(ram_1_out_9[7]));
  LED led_2 (.in(instruction_register_1_instruction_output_led[7]));
  LED led_3 (.in(clock_2_cycle_led));
  LED led_4 (.in(memory_address_register_1_memory_output_led[1]));
  LED led_5 (.in(memory_address_register_1_memory_output_led[3]));
  LED led_6 (.in(memory_address_register_1_memory_output_led[2]));
  Memory_Address_Register memory_address_register_1 (
    .Bus__Input__B0_B3(Bus), .MI(MI_t), .Clk(Clk), .Clr(Clr), .Prog(in_2), .Maual_Address_Input(in_3),
    .Address_Output(memory_address_register_1_address_output),
    .Memory_Output_LED(memory_address_register_1_memory_output_led));
  LED led_7 (.in(ram_1_out_9[6]));
  LED led_8 (.in(ram_1_out_9[3]));
  LED led_9 (.in(ram_1_out_9[4]));
  LED led_10 (.in(ram_1_out_9[5]));
  LED led_11 (.in(instruction_register_1_instruction_output_led[5]));
  LED led_12 (.in(instruction_register_1_instruction_output_led[4]));
  LED led_13 (.in(instruction_register_1_instruction_output_led[6]));
  LED led_14 (.in(instruction_register_1_instruction_output_led[3]));
  Instruction_Register instruction_register_1 (
    .Instruction_Data_input(Bus), .II(II), .Clk(Clk), .Clr(Clr), .IO(IO),
    .Optcode_output(instruction_register_1_optcode_output), .Instruction_Data_Output(Bus),
    .Instruction_Output_LED(instruction_register_1_instruction_output_led));
  LED led_15 (.in(Bus[7]));
  Clock clock_2 (
    .Clock_Input(clock_1_out), .Auto(in_1), .Step(Step), .Halt(Halt), .nClk(nClk), .Clk(Clk),
    .Cycle_Led(clock_2_cycle_led));
  LED led_16 (.in(memory_address_register_1_memory_output_led[0]));
  LED led_17 (.in(ram_1_out_9[0]));
  LED led_18 (.in(ram_1_out_9[1]));
  LED led_19 (.in(ram_1_out_9[2]));
  RAM ram_1 (
    .in_1(memory_address_register_1_address_output), .in_3(in_4), .RI(RI), .Clk(Clk), .Write(Write),
    .Prog(in_2), .RO(RO), .out_10(Bus), .out_9(ram_1_out_9), .in_2(Bus));
  LED led_20 (.in(instruction_register_1_instruction_output_led[2]));
  LED led_21 (.in(instruction_register_1_instruction_output_led[1]));
  LED led_22 (.in(instruction_register_1_instruction_output_led[0]));
  LED led_23 (.in(Bus[6]));
  LED led_24 (.in(Bus[5]));
  LED led_25 (.in(Bus[3]));
  LED led_26 (.in(Bus[4]));
  LED led_27 (.in(Bus[0]));
  LED led_28 (.in(Bus[1]));
  LED led_29 (.in(Bus[2]));
  LED led_30 (.in(registre_a_1_led_output[7]));
  LED led_31 (.in(registre_b_1_led_output[7]));
  LED led_32 (.in(out_register_1_out_led[7]));
  LED led_33 (.in(program_counter_1_out_7[3]));
  LED led_34 (.in(program_counter_1_out_7[1]));
  LED led_35 (.in(program_counter_1_out_7[2]));
  Program_Counter program_counter_1 (
    .Jump(Jump), .CE(CE), .Clk(Clk), .Clr(Clr), .CO(CO), .out_8(Bus), .out_7(program_counter_1_out_7),
    .in_1(Bus));
  LED led_36 (.in(registre_a_1_led_output[3]));
  LED led_37 (.in(registre_a_1_led_output[5]));
  LED led_38 (.in(registre_a_1_led_output[6]));
  LED led_39 (.in(registre_a_1_led_output[4]));
  Registre_A registre_a_1 (
    .Bus_Input(Bus), .in_2(AI), .in_3(AO), .in_5(Clr), .in_4(Clk), .Bus_Output(Bus),
    .ALU_Output(registre_a_1_alu_output), .Led_Output(registre_a_1_led_output));
  LED led_40 (.in(registre_b_1_led_output[3]));
  LED led_41 (.in(registre_b_1_led_output[5]));
  LED led_42 (.in(registre_b_1_led_output[4]));
  LED led_43 (.in(registre_b_1_led_output[6]));
  Registre_B registre_b_1 (
    .Bus_Input(Bus), .in_2(BI), .in_3(Clk), .in_4(Clr), .Led_Output(registre_b_1_led_output),
    .ALU_Output(registre_b_1_alu_output));
  LED led_44 (.in(out_register_1_out_led[6]));
  LED led_45 (.in(out_register_1_out_led[5]));
  LED led_46 (.in(out_register_1_out_led[3]));
  LED led_47 (.in(out_register_1_out_led[4]));
  LED led_48 (.in(program_counter_1_out_7[0]));
  LED led_49 (.in(registre_a_1_led_output[0]));
  LED led_50 (.in(registre_a_1_led_output[2]));
  LED led_51 (.in(registre_a_1_led_output[1]));
  LED led_52 (.in(registre_b_1_led_output[2]));
  LED led_53 (.in(registre_b_1_led_output[0]));
  LED led_54 (.in(registre_b_1_led_output[1]));
  LED led_55 (.in(out_register_1_out_led[0]));
  LED led_56 (.in(out_register_1_out_led[2]));
  LED led_57 (.in(out_register_1_out_led[1]));
  Out_Register out_register_1 (
    .Bus_Input(Bus), .Clk(Clk), .Output_Enable(OI), .Clr(Clr), .Digit_3(Digit_3), .Digit_2(Digit_2),
    .Digit_1(Digit_1), .Out_LED(out_register_1_out_led));
  Hex_Digit_Display hex_digit_display_1 (.value(Digit_3));  // open: dp
  LED led_58 (.in(alu_1_out_8[4]));
  LED led_59 (.in(alu_1_out_8[7]));
  LED led_60 (.in(alu_1_out_8[5]));
  LED led_61 (.in(alu_1_out_8[6]));
  ALU alu_1 (
    .A_Data_Input(registre_a_1_alu_output), .B_Data_Input(registre_b_1_alu_output), .FI(FI), .Clk(Clk),
    .Clr(Clr), .SU(SU), .out_9(Bus), .ZF(ZF), .CF(CF), .EO(EO), .out_8(alu_1_out_8));
  Hex_Digit_Display hex_digit_display_2 (.value(Digit_1));  // open: dp
  Hex_Digit_Display hex_digit_display_3 (.value(Digit_2));  // open: dp
  LED led_62 (.in(alu_1_out_8[2]));
  LED led_63 (.in(alu_1_out_8[0]));
  LED led_64 (.in(alu_1_out_8[1]));
  LED led_65 (.in(alu_1_out_8[3]));
  LED led_66 (.in(ZF));
  LED led_67 (.in(CF));

  // Other names for the same wires on the sheet: Prog = in_2; Step___Run = in_1
endmodule

module Clock (
  input  Clock_Input,
  input  Auto,
  input  Step,
  input  Halt,
  output nClk,
  output Clk,
  output Cycle_Led
);

  wire and_1_out, and_2_out, not_1_out, not_2_out, or_1_out;

  and and_1 (and_1_out, Clock_Input, Auto);
  not not_1 (not_1_out, Auto);
  and and_2 (and_2_out, not_1_out, Step);
  or or_1 (or_1_out, and_1_out, and_2_out);
  not not_2 (not_2_out, Halt);
  and and_3 (Clk, or_1_out, not_2_out);
  not not_3 (nClk, Clk);

  assign Cycle_Led = Clk;
endmodule

module Memory_Address_Register (
  input  [7:0] Bus__Input__B0_B3,
  input  MI,
  input  Clk,
  input  Clr,
  input  Prog,
  input  [3:0] Maual_Address_Input,
  output [3:0] Memory_Output_LED,
  output [3:0] Address_Output
);

  Register #(.width(4)) register_1 (.D(Bus__Input__B0_B3[3:0]), .en(MI), .Q(Memory_Output_LED), .clk(Clk), .clr(Clr));
  Multiplexer #(.width(4)) multiplexer_1 (
    .in0(Memory_Output_LED), .in1(Maual_Address_Input), .out(Address_Output), .sel(Prog));  // open: en
endmodule

module RAM (
  input  [3:0] in_1,
  input  [7:0] in_2,
  input  [7:0] in_3,
  input  RI,
  input  Clk,
  input  Write,
  input  Prog,
  input  RO,
  output [7:0] out_9,
  output [7:0] out_10
);

  wire and_1_out, multiplexer_2_out;
  wire [7:0] multiplexer_1_out;

  Multiplexer #(.width(8)) multiplexer_1 (.in0(in_2), .in1(in_3), .out(multiplexer_1_out), .sel(Prog));  // open: en
  and and_1 (and_1_out, RI, Clk);
  Multiplexer multiplexer_2 (.in0(and_1_out), .in1(Write), .out(multiplexer_2_out), .sel(Prog));  // open: en
  RAM_part #(.addrWidth(4), .bus("separate")) ram_1 (
    .addr(in_1), .din(multiplexer_1_out), .data(out_9), .clk(multiplexer_2_out), .ld(1'b1));  // open: str, sel, clr
  assign out_10 = RO ? out_9 : 8'bz;  // Controlled_Buffer controlled_buffer_1
endmodule

module Instruction_Register (
  input  [7:0] Instruction_Data_input,
  input  II,
  input  Clk,
  input  Clr,
  input  IO,
  output [7:0] Instruction_Output_LED,
  output [7:0] Instruction_Data_Output,
  output [3:0] Optcode_output
);

  wire [7:4] controlled_buffer_1_out;

  Register register_1 (.D(Instruction_Data_input), .en(II), .Q(Instruction_Output_LED), .clk(Clk), .clr(Clr));
  assign {controlled_buffer_1_out, Instruction_Data_Output[3:0]} = IO ? Instruction_Output_LED : 8'bz;  // Controlled_Buffer controlled_buffer_1
  assign Instruction_Data_Output[7:4] = IO ? 4'b0000 : 4'bz;  // Controlled_Buffer controlled_buffer_2

  assign Optcode_output = Instruction_Output_LED[7:4];
endmodule

module Registre_A (
  input  [7:0] Bus_Input,
  input  in_2,
  input  in_3,
  input  in_4,
  input  in_5,
  output [7:0] Led_Output,
  output [7:0] Bus_Output,
  output [7:0] ALU_Output
);

  Register Registre_A (.D(Bus_Input), .en(in_2), .Q(ALU_Output), .clk(in_4), .clr(in_5));
  assign Bus_Output = in_3 ? ALU_Output : 8'bz;  // Controlled_Buffer controlled_buffer_1

  assign Led_Output = ALU_Output;
endmodule

module Registre_B (
  input  [7:0] Bus_Input,
  input  in_2,
  input  in_3,
  input  in_4,
  output [7:0] Led_Output,
  output [7:0] ALU_Output
);

  Register Registre_B (.D(Bus_Input), .en(in_2), .Q(ALU_Output), .clk(in_3), .clr(in_4));

  assign Led_Output = ALU_Output;
endmodule

module ALU (
  input  [7:0] A_Data_Input,
  input  EO,
  input  [7:0] B_Data_Input,
  input  FI,
  input  Clk,
  input  Clr,
  input  SU,
  output [7:0] out_8,
  output [7:0] out_9,
  output ZF,
  output CF
);

  wire [1:0] adder_1_cout;
  wire [7:0] xor_1_out;

  xor xor_1 (xor_1_out[0], B_Data_Input[0], SU);
  xor xor_2 (xor_1_out[1], B_Data_Input[1], SU);
  xor xor_3 (xor_1_out[2], B_Data_Input[2], SU);
  xor xor_4 (xor_1_out[3], B_Data_Input[3], SU);
  xor xor_5 (xor_1_out[4], B_Data_Input[4], SU);
  xor xor_6 (xor_1_out[5], B_Data_Input[5], SU);
  xor xor_7 (xor_1_out[6], B_Data_Input[6], SU);
  xor xor_8 (xor_1_out[7], B_Data_Input[7], SU);
  Adder adder_1 (.a(A_Data_Input), .b(xor_1_out), .out(out_8), .cin(SU), .cout(adder_1_cout[0]));
  nor nor_1 (adder_1_cout[1], out_8[0], out_8[1], out_8[2], out_8[3], out_8[4], out_8[5], out_8[6], out_8[7]);
  assign out_9 = EO ? out_8 : 8'bz;  // Controlled_Buffer controlled_buffer_1
  Register #(.width(2)) register_1 (.D(adder_1_cout), .en(FI), .Q({ZF, CF}), .clk(Clk), .clr(Clr));
endmodule

module Out_Register (
  input  [7:0] Bus_Input,
  input  Clk,
  input  Output_Enable,
  input  Clr,
  output [7:0] Out_LED,
  output [3:0] Digit_3,
  output [3:0] Digit_2,
  output [3:0] Digit_1
);

  wire and_1_out;

  and and_1 (and_1_out, Clk, Output_Enable);
  Register register_1 (.D(Bus_Input), .en(1'b1), .Q(Out_LED), .clk(and_1_out), .clr(Clr));
  ROM #(.dataWidth(12)) rom_1 (.addr(Out_LED), .data({Digit_3, Digit_2, Digit_1}));  // open: sel

  // Notes on the sheet:
  //   contents of rom_1 (hex, n*v repeats v):
  //   0 1 2 3 4 5 6 7 8 9 10 11 12 13 14 15 16 17 18 19 20 21 22 23 24 25 26 27 28 29 30 31 32 33 34 35 36
  //   37 38 39 40 41 42 43 44 45 46 47 48 49 50 51 52 53 54 55 56 57 58 59 60 61 62 63 64 65 66 67 68 69
  //   70 71 72 73 74 75 76 77 78 79 80 81 82 83 84 85 86 87 88 89 90 91 92 93 94 95 96 97 98 99 100 101
  //   102 103 104 105 106 107 108 109 110 111 112 113 114 115 116 117 118 119 120 121 122 123 124 125 126
  //   127 128 129 130 131 132 133 134 135 136 137 138 139 140 141 142 143 144 145 146 147 148 149 150 151
  //   152 153 154 155 156 157 158 159 160 161 162 163 164 165 166 167 168 169 170 171 172 173 174 175 176
  //   177 178 179 180 181 182 183 184 185 186 187 188 189 190 191 192 193 194 195 196 197 198 199 200 201
  //   202 203 204 205 206 207 208 209 210 211 212 213 214 215 216 217 218 219 220 221 222 223 224 225 226
  //   227 228 229 230 231 232 233 234 235 236 237 238 239 240 241 242 243 244 245 246 247 248 249 250 251
  //   252 253 254 255
endmodule

module Program_Counter (
  input  [7:0] in_1,
  input  Jump,
  input  CE,
  input  Clk,
  input  Clr,
  input  CO,
  output [3:0] out_7,
  output [7:0] out_8
);

  wire [7:4] counter_1_q;

  Counter #(.max('hf)) counter_1 (
    .load(Jump), .D(in_1), .count(CE), .Q({counter_1_q, out_7}), .clk(Clk), .clr(Clr));  // open: carry
  assign out_8 = CO ? {counter_1_q, out_7} : 8'bz;  // Controlled_Buffer controlled_buffer_1

  // Notes on the sheet:
  //   /!\ --- Valeur de comptage max 0x0f --- /!\
endmodule

module Control_Logic (
  input  Clk,
  input  [3:0] Optcode_Input,
  input  Carry,
  input  Clr,
  input  Zero,
  output [4:0] Cycle_Led,
  output AI,
  output AO,
  output BI,
  output FI,
  output EO,
  output SU,
  output CO,
  output CE,
  output Jump,
  output RI,
  output RO,
  output Halt,
  output OI,
  output MI,
  output II,
  output IO
);

  wire [3:0] counter_1_q;

  Counter #(.width(4), .max('h4)) counter_1 (.Q(counter_1_q), .clk(Clk), .clr(Clr));  // open: load, D, count, carry
  Decoder #(.select(4)) decoder_1 (
    .out0(Cycle_Led[4]), .out1(Cycle_Led[3]), .out2(Cycle_Led[2]), .out3(Cycle_Led[1]), .out4(Cycle_Led[0]),
    .sel(counter_1_q));  // open: out5, out6, out7, out8, out9, out10, out11, out12, out13, out14, out15, en
  ROM #(.addrWidth(10), .dataWidth(16)) rom_1 (
    .addr({Zero, Carry, counter_1_q, Optcode_Input}),
    .data({IO, II, MI, OI, Halt, RO, RI, Jump, CE, CO, SU, EO, FI, BI, AO, AI}));  // open: sel

  // Notes on the sheet:
  //   contents of rom_1 (hex, n*v repeats v):
  //   16*2040 16*4480 0 a000 a000 a000 8001 8004 8004 a000 0 0 8100 8100 0 8100 1002 800 0 401 404 404 0
  //   19 39 202 10*0 19 39 188*0 16*2040 16*4480 0 a000 a000 a000 8001 8004 8004 a000 8100 0 0 8100 0 8100
  //   1002 800 0 401 404 404 0 19 39 202 10*0 19 39 188*0 16*2040 16*4480 0 a000 a000 a000 8001 8004 8004
  //   a000 0 8100 8100 0 0 8100 1002 800 0 401 404 404 0 19 39 202 10*0 19 39 188*0 16*2040 16*4480 0 a000
  //   a000 a000 8001 8004 8004 a000 8100 8100 0 0 0 8100 1002 800 0 401 404 404 0 19 39 202 10*0 19 39
  //   /!\ L'entrée horloge doit être inversé de manière a positionner les bits ENTRE chaque cycle d'horloge
endmodule
